# Fritzing sketch half-bridge-driver (saved by Fritzing 0.9.2b)
circuit board: 3.8cm x 3.8cm
breadboards: 1

parts:
  C2 = Ceramic Capacitor [capacitance=100nF package="100 mil [THT, multilayer]"]
  C3 = Ceramic Capacitor [capacitance=100nF package="100 mil [THT, multilayer]"]
  D1 = Rectifier Diode [part_number=1N4001 package="300 mil [THT]"]
  R1 = Resistor [tolerance=±5% resistance=10 package=THT]
  R2 = Resistor [tolerance=±5% resistance=10 package=THT]
  Q1 = Basic FET N-Channel [part_number=IRFZ44 package="TO220 [THT]"]
  Q2 = Basic FET N-Channel [part_number=IRFZ44 package="TO220 [THT]"]
  Motor1 = screw terminal, 3 pins
  IC1 = IC, DIP package, 8 pins [chip_label=IC part_number=IR2184]
  J1 = male pin header, 3 pins [form="♂ (male)"]
  J3 = female pin header, 2 pins [form="♀ (female)"]
  24V = Screw terminal - 2 pins [package=THT]
  C1 = Electrolytic Capacitor [capacitance=1mF voltage=50V package="200 mil [THT, electrolytic]"]
  12V = Screw terminal - 2 pins [package=THT]

nets:
  N1: C2.0, Q1.drain, Q2.source, Motor1.pin2, IC1.pin6
  N2: C2.1, D1.cathode, IC1.pin8
  GND: C3.0, Q1.source, Motor1.pin3, IC1.pin4, J1.pin3, 24V.pin2, C1.-, 12V.pin1
  12V: C3.1, D1.anode, IC1.pin1, J3.pin1, 12V.pin2
  N3: R1.Pin_0, IC1.pin7
  N4: R1.Pin_1, Q2.gate
  N5: R2.Pin_0, IC1.pin5
  N6: R2.Pin_1, Q1.gate
  24V: Q2.drain, Motor1.pin1, J3.pin2, 24V.pin1, C1.+
  N7: IC1.pin2, J1.pin1
  N8: IC1.pin3, J1.pin2

notes:
  Half bridge
  V 1.0
  https://www.mikrocontroller.net/articles/Motoransteuerung_mit_PWM#2-Quadrantensteller_mit_Halbbr.C3.BCcken_Mosfettreiber
