# Fritzing sketch induction-sensor (saved by Fritzing 0.9.2b)
circuit board: 8.46667cm x 5.64444cm
breadboards: 1

parts:
  R1 = Resistor [tolerance=±5% resistance=10k package=THT]
  R2 = Resistor [tolerance=±5% resistance=47k package=THT]
  R3 = Resistor [tolerance=±5% resistance=10k package=THT]
  R4 = Resistor [tolerance=±5% resistance=470 package=THT]
  R5 = Resistor [tolerance=±5% resistance=330 package=THT]
  R6 = Resistor [tolerance=±5% resistance=4.7k package=THT]
  R7 = Resistor [tolerance=±5% resistance=1M package=THT]
  R8 = Resistor [tolerance=±5% resistance=4.7k package=THT]
  R9 = Trimmer Potentiometer [maximum_resistance=100kΩ package=THT]
  IC1 = IC, DIP package, 8 pins [chip_label=IC part_number=LM358]
  D1 = Rectifier Diode [part_number=1N4148 package="300 mil [THT]"]
  D2 = Rectifier Diode [part_number=1N4148 package="300 mil [THT]"]
  L1 = Inductor [package="400 mil [THT]"]
  C1 = Electrolytic Capacitor [capacitance=1µF package="100 mil [THT, electrolytic]"]
  J1 = female pin header, 4 pins [form="♀ (female)"]
  C2 = Ceramic Capacitor [capacitance=100nF package="100 mil [THT, multilayer]"]

nets:
  N1: R1.Pin_0, R2.Pin_0, D1.cathode, D2.anode, L1.pin_0
  N2: R1.Pin_1, IC1.pin3
  N3: R2.Pin_1, R3.Pin_0, R4.Pin_1, R5.Pin_0, R6.Pin_1, D1.anode, D2.cathode, L1.pin_1
  N4: R3.Pin_1, R9.leg1, R9.wiper, IC1.pin2
  5V: R4.Pin_0, IC1.pin8, J1.pin1, C2.1
  GND: R5.Pin_1, IC1.pin4, C1.-, J1.pin4, C2.0
  N5: R6.Pin_0, R7.Pin_0, IC1.pin5
  N6: R7.Pin_1, R8.Pin_0, IC1.pin7, J1.pin2
  N7: R8.Pin_1, C1.+, J1.pin3
  N8: R9.leg2, IC1.pin1, IC1.pin6

notes:
  Puls
  DC
  I
