# Fritzing sketch induction-transmitter (saved by Fritzing 0.9.2b)
circuit board: 8.46667cm x 5.64444cm
breadboards: 1

parts:
  Q1 = Basic FET N-Channel [part_number=IRFZ3205 package="TO220 [THT]"]
  R1 = Resistor [tolerance=±5% resistance=100 package=THT]
  R2 = Resistor [tolerance=±5% resistance=10k package=THT]
  R3 = Resistor [tolerance=±5% resistance=330 package=THT]
  R4 = Resistor [tolerance=±5% resistance=120 package=THT]
  R5 = Resistor [tolerance=±5% resistance=24 power=4W package=THT]
  C1 = Ceramic Capacitor [capacitance=10nF voltage=16V package="100 mil [THT, multilayer]"]
  C3 = Electrolytic Capacitor [capacitance=1mF voltage=50V package="100 mil [THT, electrolytic]"]
  R6 = Rotary Potentiometer (Small) [maximum_resistance=1kΩ package=THT]
  IC1 = IC, DIP package, 8 pins [chip_label=IC part_number=NE555]
  Jumper = male pin header, 2 pins [form="♂ (male)"]
  Power_plug1 = Power plug
  K2 = Screw terminal - 2 pins [package=THT]
  K1 = screw terminal, 3 pins
  D1 = Rectifier Diode [part_number=1N4148 package="300 mil [THT]"]
  D2 = Rectifier Diode [part_number=1N4148 package="300 mil [THT]"]
  C4 = Electrolytic Capacitor [capacitance=10µF voltage=16V package="100 mil [THT, electrolytic]"]
  C2 = Ceramic Capacitor [capacitance=470nF voltage=16V package="100 mil [THT, multilayer]"]

nets:
  N1: Q1.gate, R1.Pin_0
  N2: Q1.drain, K2.pin2
  GND: Q1.source, C1.0, C3.-, IC1.pin1, Power_plug1.GND, K1.pin3, C4.-, C2.0
  N3: R1.Pin_1, R4.Pin_0, IC1.pin3
  N4: R2.Pin_0, R4.Pin_1, R6.leg1, R6.wiper
  12V: R2.Pin_1, IC1.pin4, IC1.pin8, Jumper.pin1, Power_plug1.VCC, K1.pin1, C4.+
  N5: R3.Pin_0, R6.leg2, IC1.pin7, D2.anode
  N6: R3.Pin_1, D1.cathode
  20V: R5.Pin_0, Jumper.pin2, K1.pin2
  N7: R5.Pin_1, C3.+, K2.pin1
  N8: C1.1, IC1.pin5
  N9: IC1.pin2, IC1.pin6, D1.anode, D2.cathode, C2.1

notes:
  http://rn-wissen.de/wiki/index.php/Begrenzungsschleife_-_Induktionsschleife
  schleife
  I
